# Fritzing sketch Raspberry Pi Camera (saved by Fritzing 0.9.2b)
breadboards: 1

parts:
  Raspberry_Pi1 = Raspberry Pi 2
  S1 = SWITCH-MOMENTARY-2 [package=tactile-pth-12mm]
  Pi1 = Adafruit Pi Cobbler
  J1 = Cobbler Plus Cable
  R1 = Resistor [tolerance=±5% resistance=10k package="2512 [SMD]"]

nets:
  3V3: Raspberry_Pi1.3v3, Raspberry_Pi1.3V3, J1.3.3V#41, J1.3.3V#57
  N1: Raspberry_Pi1.GPIO2, J1.GPIO_2
  N2: Raspberry_Pi1.GPIO3, J1.GPIO_3
  N3: Raspberry_Pi1.GPIO4, J1.GPIO_4
  N4: Raspberry_Pi1.GND, J1.GND#46, J1.GND#49, J1.GND#54, J1.GND#60, J1.GND#65, J1.GND#70, J1.GND#74, J1.GND#79
  N5: Raspberry_Pi1.GPIO17, J1.GPIO_17
  N6: Raspberry_Pi1.GPIO27, J1.GPIO_27
  N7: Raspberry_Pi1.GPIO22, J1.GPIO_22
  N8: Raspberry_Pi1.GPIO10, J1.GPIO_10
  N9: Raspberry_Pi1.GPIO9, J1.GPIO_9
  N10: Raspberry_Pi1.GPIO11, J1.GPIO_11
  N11: Raspberry_Pi1.ID_SD, J1.ID_SD
  N12: Raspberry_Pi1.GPIO5, J1.GPIO_5
  N13: Raspberry_Pi1.GPIO6, J1.GPIO_6
  N14: Raspberry_Pi1.GPIO13, J1.GPIO_13
  N15: Raspberry_Pi1.GPIO19, J1.GPIO_19
  N16: Raspberry_Pi1.GPIO26, J1.GPIO_26
  N17: Raspberry_Pi1.GPIO21, J1.GPIO_21
  N18: Raspberry_Pi1.GPIO20, J1.GPIO_20
  N19: Raspberry_Pi1.GPIO16, J1.GPIO_16
  N20: Raspberry_Pi1.GPIO12, J1.GPIO_12
  N21: Raspberry_Pi1.ID_SC, J1.ID_SC
  N22: Raspberry_Pi1.GPIO7, J1.GPIO_7
  N23: Raspberry_Pi1.GPIO8, J1.GPIO_8
  N24: Raspberry_Pi1.GPIO25, J1.GPIO_25
  N25: Raspberry_Pi1.GPIO24, J1.GPIO_24
  N26: Raspberry_Pi1.GPIO23, J1.GPIO_23
  N27: Raspberry_Pi1.GPIO18, J1.GPIO_18
  N28: Raspberry_Pi1.GPIO15, J1.GPIO_15
  N29: Raspberry_Pi1.GPIO14, J1.GPIO_14
  5V: Raspberry_Pi1.5V, J1.5V
  N30: S1.2, Pi1.PIN4, J1.5.0V#3
  3V3_2: Pi1.3V3, J1.3V3
  N31: Pi1.5V0, J1.5.0V#1
  N32: Pi1.SDA0, J1.SDA
  N33: Pi1.SCL0, J1.SCL
  N34: Pi1.GND, J1.GND#5
  N35: Pi1.#4, J1.#4
  N36: Pi1.TXD, J1.TXD
  N37: Pi1.PIN9, J1.GND#8
  N38: Pi1.RXD, J1.RXD
  N39: Pi1.#17, J1.#17
  N40: Pi1.#18, J1.#18
  N41: Pi1.#21, J1.#27
  N42: Pi1.PIN14, J1.GND#13
  N43: Pi1.#22, J1.#22
  N44: Pi1.#23, J1.#23, R1.Pin_1
  N45: Pi1.PIN19, J1.3.3V#16
  N46: Pi1.#24, J1.#24
  N47: Pi1.MOSI, J1.MOSI
  N48: Pi1.PIN20, J1.GND#19, R1.Pin_0
  N49: Pi1.MISO, J1.MISO
  N50: Pi1.#25, J1.#25
  N51: Pi1.SCLK, J1.SCLK
  N52: Pi1.CE0, J1.CE0
  N53: Pi1.PIN25, J1.GND#24
  N54: Pi1.CE1, J1.CE1

notes:
  ↑↑ Connect your camera to this input, bare pins facing away from the ethernet jack
  note that resistor value isn't terribly important here. something in the 10-50Kohm range is typical, but just about anything will likely be fine.

custom parts:
  Adafruit Pi Cobbler: Adafruit Pi Cobbler GPIO Breakout for Raspberry Pi
  Cobbler Plus Cable: The Cobbler Plus is an add on prototyping board from Adafruit specifically designed for the Raspberry Pi B+ that can break out all those tasty power, GPIO, I2C and SPI pins from the 40-pin header onto a solderless breadboard. This set will make "cobbling together" prototypes with the Pi super easy. The Cobbler Plus can plug into any solderless breadboard.
